# Fritzing sketch smartPlantFritzingLayout (saved by Fritzing 1.0.0rc)
breadboards: 1

parts:
  A1 = Particle - Photon2
  Part1 = MQ-131 breakout
  Grove1 = Grove Dust Sensor
  J1 = Camdenboss CTB0158-3 [part_number=CTB0158-3 package=THT]
  J2 = Camdenboss CTB0158-3 [part_number=CTB0158-3 package=THT]  # not connected
  J3 = Camdenboss CTB0158-3 [part_number=CTB0158-3 package=THT]
  J4 = Camdenboss CTB0158-4 [part_number=CTB0158-4 package=THT]  # not connected
  Q1 = TRANSISTOR_PNP [package=to-92]
  R3 = Resistor [tolerance=±5% resistance=3.3k package="1206 [SMD]"]
  R4 = Resistor [tolerance=±5% resistance=1.8k package="0603 [SMD]"]
  Chirp!_Soil_Moisture_Sensor1 = Chirp! Soil Moisture Sensor v2.7.3

nets:
  N1: A1.Pin_2, Chirp!_Soil_Moisture_Sensor1.pin_2
  N2: A1.Pin_4, Q1.C, Chirp!_Soil_Moisture_Sensor1.pin_4
  N3: A1.Pin_6, Chirp!_Soil_Moisture_Sensor1.Pin_0
  N4: A1.Pin_7, Grove1.NC, J3.pin1
  N5: A1.Pin_8, Part1.AO, J1.pin3
  N6: A1.Pin_26, Grove1.VCC, J3.pin2, R4.Pin_1
  N7: Part1.VCC, J1.pin1
  N8: Part1.GND, J1.pin2
  N9: Grove1.GND, J3.pin3
  N10: Q1.E, R4.Pin_0
  N11: Q1.B, R3.Pin_0

custom parts:
  Particle - Photon2: The Photon 2 is a microcontroller and Wi-Fi networking developed by particle. Features: 802.11a/b/g/n Wi-Fi, 2.4 GHz and 5 GHz Integrated PCB antenna Integrated U.FL connector for external antenna Integrated RF switch BLE 5 using same antenna as Wi-Fi Realtek RTL8721DM MCU ARM Cortex M33 CPU, 200 MHz 2048 KB (2 MB) user application maximum size 3072 KB (3 MB) of RAM available to user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
  MQ-131 breakout: SKU: 101282
  Grove Dust Sensor: PPD42 Grove Dust Sensor
